// Logisim project Decoder.circ as structural Verilog
module main (
  input  in_1,
  input  O2,
  input  in_3,
  output out_4,
  output out_5,
  output out_6,
  output out_7,
  output out_8,
  output out_9,
  output out_10
);

  wire A_out, and_1_out, and_2_out, and_3_out, and_4_out, and_5_out, and_6_out, and_7_out, B_out, C_out,
       D_out, E_out, F_out, G_out, not_1_out, not_2_out, not_3_out, not_4_out, not_6_out, not_7_out,
       not_8_out, not_9_out, not_10_out, not_11_out, not_12_out;

  not not_1 (not_1_out, in_1);
  not not_2 (not_2_out, O2);
  not not_3 (not_3_out, in_3);
  not not_4 (not_4_out, in_1);
  not not_5 (in_3, O2);
  not not_6 (not_6_out, in_1);
  not not_7 (not_7_out, in_3);
  not not_8 (not_8_out, in_1);
  not not_9 (not_9_out, O2);
  not not_10 (not_10_out, in_3);
  not not_11 (not_11_out, O2);
  not not_12 (not_12_out, in_3);
  _7_Segment_Display u_7_segment_display_1 ();  // open: g, f, a, b, e, d, c, dp
  and and_1 (and_1_out, not_1_out, not_2_out, not_3_out);
  and and_2 (and_2_out, not_4_out, in_3, in_3);
  and and_3 (and_3_out, not_6_out, O2, not_7_out);
  and and_4 (and_4_out, not_8_out, O2, in_3);
  and and_5 (and_5_out, in_1, not_9_out, not_10_out);
  and and_6 (and_6_out, in_1, not_11_out, in_3, in_3);
  and and_7 (and_7_out, in_1, O2, not_12_out);
  or A (A_out, and_1_out, and_3_out, and_4_out);
  or B (B_out, and_1_out, and_2_out, and_3_out, and_4_out, and_5_out);
  or C (C_out, and_1_out, and_2_out, and_4_out, and_5_out);
  or D (D_out, and_1_out, and_3_out, and_4_out);
  or E (E_out, and_1_out, and_3_out);
  or F (F_out, and_1_out, and_5_out);
  or G (G_out, and_3_out, and_4_out, and_5_out);
  or A_2 (out_4, and_6_out, and_7_out, A_out);
  buf B_2 (out_5, B_out);  // OR_Gate
  or C_2 (out_6, and_6_out, and_7_out, C_out);
  or D_2 (out_7, and_6_out, and_7_out, D_out);
  or E_2 (out_8, and_7_out, E_out);
  or F_2 (out_9, and_6_out, and_7_out, F_out);
  or G_2 (out_10, and_6_out, and_7_out, G_out);

  // Notes on the sheet:
  //   O1
  //   O3
  //   Motor Car
  //   Car1
  //   Car2
  //   Car3
  //   Car4
  //   Car5
  //   Car6
  //   Decoder
endmodule
