// Logisim project Encoder.circ as structural Verilog: 1 circuit, main circuit main
module main (
);

  wire or_1_out, or_2_out, or_3_out, undriven, undriven_2, undriven_3, undriven_4, undriven_5, undriven_6;

  or or_1 (or_1_out, undriven, undriven_4, undriven_2);
  or or_2 (or_2_out, undriven_5, undriven_2, undriven_3);
  or or_3 (or_3_out, undriven, undriven_3, undriven_6);

  // Notes on the sheet:
  //   I5
  //   I3
  //   I6
  //   I1
  //   I2
  //   Encoder
  //   I4
endmodule
