// Logisim project p1a.circ as structural Verilog: 1 circuit, main circuit main
module main (
);

  wire and_1_out, and_2_out, or_1_out, or_2_out, or_3_out, undriven, undriven_2, undriven_3;

  and and_1 (and_1_out, undriven_2, undriven_3);
  and and_2 (and_2_out, and_1_out, undriven);
  or or_1 (or_1_out, and_1_out, and_2_out);
  or or_2 (or_2_out, undriven_2, or_1_out);
  or or_3 (or_3_out, or_2_out, undriven_3);
  // OR_Gate or_4 has open pins: in1=or_3_out, in2=undriven, out=open

  // Notes on the sheet:
  //   A
  //   B
  //   C
endmodule
