// Logisim project p1b.circ as structural Verilog: 1 circuit, main circuit main
module main (
);

  wire and_1_out, and_2_out, and_3_out, and_4_out, and_5_out, and_6_out, not_1_out, not_2_out, not_3_out,
       or_1_out, undriven, undriven_2, undriven_3, undriven_4, undriven_5, undriven_6, undriven_7,
       undriven_8, undriven_9;

  not not_1 (not_1_out, undriven);
  not not_2 (not_2_out, undriven_2);
  not not_3 (not_3_out, undriven_3);
  and and_1 (and_1_out, not_1_out, not_2_out, not_2_out);
  and and_2 (and_2_out, undriven_4, undriven_5);
  and and_3 (and_3_out, undriven_7, undriven_8);
  and and_4 (and_4_out, and_1_out, undriven_9);
  and and_5 (and_5_out, not_3_out, and_2_out);
  and and_6 (and_6_out, undriven_6, and_3_out);
  or or_1 (or_1_out, and_4_out, and_5_out);
  // OR_Gate or_2 has open pins: in1=or_1_out, in3=and_6_out, out=open

  // Notes on the sheet:
  //   A
  //   B
  //   C
  //   C
  //   A
  //   B
  //   A
  //   B
  //   C
endmodule
