// Logisim project p1c.circ as structural Verilog: 1 circuit, main circuit main
module main (
);

  wire and_1_out, and_2_out, and_3_out, not_1_out, not_2_out, not_3_out, or_1_out, undriven, undriven_2,
       undriven_3, undriven_4, undriven_5, undriven_6;

  // NOT_Gate not_1 has open pins: in=open, out=not_1_out
  // NOT_Gate not_2 has open pins: in=open, out=not_2_out
  // NOT_Gate not_3 has open pins: in=open, out=not_3_out
  and and_1 (and_1_out, not_1_out, not_1_out, not_2_out, undriven);
  and and_2 (and_2_out, undriven_2, undriven_3, not_3_out, not_3_out);
  and and_3 (and_3_out, undriven_4, undriven_5, undriven_6);
  or or_1 (or_1_out, and_1_out, and_2_out);
  // OR_Gate or_2 has open pins: in1=or_1_out, in3=and_3_out, out=open

  // Notes on the sheet:
  //   A
  //   B
  //   C
  //   A
  //   B
  //   C
  //   A
  //   B
  //   C
endmodule
