// Logisim project p2.2.circ as structural Verilog: 3 circuits, main circuit main
module main (
);

  wire button_1_out, flipflop_1_out_3, not_1_out;

  Button button_1 (.out(button_1_out));
  flipflop flipflop_1 (.in_1(not_1_out), .in_2(button_1_out), .out_3(flipflop_1_out_3));
  not not_1 (not_1_out, flipflop_1_out_3);
  LED led_1 (.in(flipflop_1_out_3));

  // Notes on the sheet:
  //   741G04
  //   7411
  //   7427
endmodule

module latch (
  input  in_1,
  input  in_2,
  output out_3
);

  wire and_1_out, and_2_out, nor_1_out, not_1_out;

  not not_1 (not_1_out, in_1);
  and and_1 (and_1_out, in_1, in_2);
  and and_2 (and_2_out, in_2, not_1_out);
  nor nor_1 (nor_1_out, and_1_out, out_3);
  nor nor_2 (out_3, nor_1_out, and_2_out);
endmodule

module flipflop (
  input  in_1,
  input  in_2,
  output out_3
);

  wire latch_1_out_3, not_1_out;

  latch latch_1 (.in_1(in_1), .in_2(in_2), .out_3(latch_1_out_3));
  not not_1 (not_1_out, in_2);
  latch latch_2 (.in_1(latch_1_out_3), .in_2(not_1_out), .out_3(out_3));
endmodule
