// Logisim project hw2.3.32.circ as structural Verilog: 1 circuit, main circuit main
module main (
);

  wire and_1_out, and_2_out, and_3_out, and_4_out, and_5_out, and_6_out, not_1_out, not_2_out, not_3_out,
       not_4_out, or_1_out, or_2_out, undriven, undriven_2, undriven_3, undriven_4, xor_1_out;

  not not_1 (not_1_out, undriven_2);
  not not_2 (not_2_out, undriven);
  not not_3 (not_3_out, undriven_3);
  not not_4 (not_4_out, undriven_4);
  and and_1 (and_1_out, not_1_out, not_2_out, not_3_out, not_4_out);
  and and_2 (and_2_out, undriven_2, undriven_4, not_3_out);
  and and_3 (and_3_out, not_4_out, undriven_4);
  and and_4 (and_4_out, not_1_out, not_4_out, not_3_out, undriven);
  and and_5 (and_5_out, not_1_out, not_3_out, undriven_4);
  and and_6 (and_6_out, undriven, undriven_3, not_4_out);
  xor xor_1 (xor_1_out, undriven_3, undriven_4);
  or or_1 (or_1_out, and_1_out, and_2_out, and_3_out);
  or or_2 (or_2_out, and_4_out, and_5_out, and_6_out);

  // Notes on the sheet:
  //   A
  //   B
  //   S1
  //   S0
  //   Y
  //   N0
  //   N1
endmodule
